// Logisim project Lab5_Asher_Wu.circ as structural Verilog: 2 circuits, main circuit main
module main (
  input  Input_1,
  input  Input_2,
  input  Input_3,
  output Output_1,
  output Output_2
);

  FA FA_1 (.Input_1(Input_1), .Input_2(Input_2), .C_in(Input_3), .S(Output_1), .Output_1(Output_2));
endmodule

module FA (
  input  Input_1,
  input  Input_2,
  input  C_in,
  output S,
  output Output_1
);

  wire and_1_out, and_2_out, xor_1_out;

  xor xor_1 (xor_1_out, Input_1, Input_2);
  xor xor_2 (S, xor_1_out, C_in);
  and and_1 (and_1_out, xor_1_out, C_in);
  and and_2 (and_2_out, Input_1, Input_2);
  or or_1 (Output_1, and_1_out, and_2_out);
endmodule
